# Fritzing sketch Galileo Blink with External LED (saved by Fritzing 0.9.0b)

parts:
  Part1 = Intel Galileo
  LED1 = LED - 5mm [color="Red (633nm)" package="5 mm [THT]"]

nets:
  N1: Part1.D13/SCK, LED1.anode
  N2: Part1.GND, LED1.cathode

notes:
  Anode (long leg)
  Cathode (short leg)
