# Fritzing sketch RGB LED Model (saved by Fritzing 0.9.0b)

parts:
  Part1 = Intel Galileo
  RGB_LED = Super Flux RGB LED (com. anode)
  R1 = Resistor [tolerance=±5% resistance=150 package=THT]
  R2 = Resistor [tolerance=±5% resistance=91 package=THT]
  R3 = Resistor [tolerance=±5% resistance=91 package=THT]

nets:
  N1: Part1.D9_PWM, R1.Pin_1
  N2: Part1.D10_PWM/SS, R2.Pin_1
  N3: Part1.D3_PWM, R3.Pin_1
  N4: Part1.5V, RGB_LED.common_anode
  N5: RGB_LED.red_cathode, R1.Pin_0
  N6: RGB_LED.blue_cathode, R3.Pin_0
  N7: RGB_LED.green_cathode, R2.Pin_0
